# Fritzing sketch droneckt (saved by Fritzing 0.9.5d)

parts:
  M1 = STM32F103C8T6 blue mini board
  U1 = MPU 9250 Breakout [package="SIP (Single Inline) [THT]"]
  Mod1 = flyskyr6b
  A1 = DYS BE1806
  A2 = Littlebee 20A ESC
  C1 = Capacitor [package=cap-pth-small-kit]
  C2 = Tantalum Capacitor [capacitance=10µF voltage=16V package="100 mil [THT, tantalum]"]
  C3 = Capacitor Polarized [package=cpol-radial-100uf-25v]
  C4 = Capacitor Polarized [package=cpol-radial-1000uf-25v]
  A3 = PDB500
  U2 = LIPO-2000mAh [package=lipo-2000]
  A4 = DYS BE1806
  A5 = DYS BE1806
  A6 = DYS BE1806
  A7 = Littlebee 20A ESC
  A8 = Littlebee 20A ESC
  A9 = Littlebee 20A ESC
  C5 = Capacitor [package=cap-pth-small-kit]

nets:
  N1: M1.B12, Mod1.CH5
  N2: M1.B13, Mod1.CH6
  N3: M1.A8, Mod1.CH1
  N4: M1.A9, Mod1.CH2
  N5: M1.A10, Mod1.CH3
  N6: M1.A11, Mod1.CH4
  N7: M1.5V, C3.+, A3.Pin_36
  N8: M1.G, M1.GND, C3.-, A3.Pin_35
  N9: M1.A0, A7.Pin_7
  N10: M1.A1, A2.Pin_7
  N11: M1.A2, A8.Pin_7
  N12: M1.A3, A9.Pin_7
  N13: M1.A4, U1.NCS
  N14: M1.A5, U1.SCL
  N15: M1.A6, U1.AD0
  N16: M1.A7, U1.SDA
  N17: M1.B0, U1.INT
  N18: U1.VCC, C1.1, C2.-, C5.2
  N19: U1.GND, C1.2, C2.+, C5.1
  N20: Mod1.VCC, Mod1.BAT+, A3.Pin_33
  N21: Mod1.connector14, Mod1.GND, A3.Pin_32
  N22: A1.Pin_1, A8.Pin_5
  N23: A1.Pin_2, A8.Pin_4
  N24: A1.Pin_3, A8.Pin_3
  N25: A2.Pin_1, A3.Pin_1
  N26: A2.Pin_2, A3.Pin_5
  N27: A2.Pin_3, A6.Pin_3
  N28: A2.Pin_4, A6.Pin_2
  N29: A2.Pin_5, A6.Pin_1
  N30: C4.+, A3.Pin_17, U2.-
  N31: C4.-, A3.Pin_18, U2.+
  N32: A3.Pin_12, A8.Pin_1
  N33: A3.Pin_16, A8.Pin_2
  N34: A3.Pin_19, A9.Pin_1
  N35: A3.Pin_23, A9.Pin_2
  N36: A3.Pin_37, A7.Pin_1
  N37: A3.Pin_41, A7.Pin_2
  N38: A4.Pin_1, A9.Pin_5
  N39: A4.Pin_2, A9.Pin_4
  N40: A4.Pin_3, A9.Pin_3
  N41: A5.Pin_1, A7.Pin_5
  N42: A5.Pin_2, A7.Pin_4
  N43: A5.Pin_3, A7.Pin_3

custom parts:
  MPU 9250 Breakout: Generic MPU 9250 Breakout Board
  flyskyr6b: flysky r6b 6ch rc receiver module. Pcb view is 3*7 header pins, 3 female headers will let the board plug in to the receiver, or connect via wires as you choose.
  DYS BE1806: quadcopter brushless motor.
  Littlebee 20A ESC: LittleBee 20A 2-4 LiPo Battery OPTO ESC Brushless Speed Controller for RC FPV Multicopter.
  PDB500: The PDB500 is designed for high voltage and high current applications. It consists of 8 layers of heavy copper to sustain maximum current demand whilst dissipating minimal heat.
